# Fritzing sketch sketch (saved by Fritzing 0.8.5b)
circuit board: 13.2278cm x 7.11468cm

parts:
  RE1 = Rotary Encoder [package=THT]
  R1 = Resistor [tolerance=±5% resistance=10k package=THT]
  RIT = Pushbutton [package="[THT]"]
  NO_FUNC_YET = Pushbutton [package="[THT]"]
  MODE = Pushbutton [package="[THT]"]
  VFO_A/B = Pushbutton [package="[THT]"]
  Encoder_Push_Button = Pushbutton [package="[THT]"]
  R3 = Resistor [tolerance=±5% resistance=4.7k package=THT]
  R4 = Resistor [tolerance=±5% resistance=2.2k package=THT]
  C1 = Ceramic Capacitor [capacitance=100nF package="100 mil [THT, multilayer]"]
  C4 = Ceramic Capacitor [capacitance=100nF package="100 mil [THT, multilayer]"]
  C3 = Ceramic Capacitor [capacitance=100nF package="100 mil [THT, multilayer]"]
  C2 = Ceramic Capacitor [capacitance=100nF package="100 mil [THT, multilayer]"]
  C5 = Ceramic Capacitor [capacitance=100nF package="100 mil [THT, multilayer]"]
  R5 = Trimmer Potentiometer [maximum_resistance=10kΩ package=THT]
  R6 = Resistor [tolerance=±5% resistance=470 package=THT]
  R2 = Resistor [tolerance=±5% resistance=10k package=THT]
  LCD1 = LCD screen
  Parte1 = Arduino Uno (Rev3)
  JP3 = Header 4 [package=screwterminal-3.5mm-4_lock]
  JP4 = Header 3 [package=molex-1x3_lock]
  U1 = TLP621 [package=THT]
  R7 = Resistor [tolerance=±5% resistance=220 package=THT]
  JP5 = Header 3 [package=molex-1x3_lock]
  JP6 = Header 3 [package=molex-1x3_lock]
  JP7 = Header 3 [package=molex-1x3_lock]

nets:
  N1: RE1.EncoderPinA, Parte1.D2
  VSS: RE1.EncoderPinC, RIT.Pin_3, RIT.Pin_4, NO_FUNC_YET.Pin_3, NO_FUNC_YET.Pin_4, MODE.Pin_3, MODE.Pin_4, VFO_A/B.Pin_3, VFO_A/B.Pin_4, Encoder_Push_Button.Pin_3, Encoder_Push_Button.Pin_4, C1.0, C4.0, C3.0, C2.0, C5.0, R5.leg2, R6.Pin_0, LCD1.VSS, LCD1.R/W, LCD1.LED+, Parte1.GND, JP3.1, JP4.3, U1.Pin_2, U1.Pin_3, JP5.3, JP6.3, JP7.3
  N2: RE1.EncoderPinB, Parte1.D3_PWM
  VDD: R1.Pin_0, R5.leg1, LCD1.VDD, Parte1.5V, JP3.2
  N3: R1.Pin_1, NO_FUNC_YET.Pin_1, NO_FUNC_YET.Pin_2, R3.Pin_0, R4.Pin_0, C1.1, R2.Pin_0, Parte1.A2
  N4: RIT.Pin_1, RIT.Pin_2, R4.Pin_1, C4.1
  N5: MODE.Pin_1, MODE.Pin_2, R3.Pin_1, C3.1
  N6: VFO_A/B.Pin_1, VFO_A/B.Pin_2, C2.1, R2.Pin_1
  N7: Encoder_Push_Button.Pin_1, Encoder_Push_Button.Pin_2, C5.1, Parte1.D4
  N8: R5.wiper, LCD1.V0
  N9: R6.Pin_1, LCD1.LED-
  N10: LCD1.RS, Parte1.D8
  N11: LCD1.E, Parte1.D7
  N12: LCD1.DB4, Parte1.D6_PWM
  N13: LCD1.DB5, Parte1.D5_PWM
  N14: LCD1.DB6, Parte1.D10_PWM/SS
  N15: LCD1.DB7, Parte1.D9_PWM
  N16: Parte1.A0, JP4.1
  N17: Parte1.A1, JP6.1
  N18: Parte1.A4/SDA, JP3.3
  N19: Parte1.A5/SCL, JP3.4
  N20: Parte1.D13/SCK, U1.Pin_4
  N21: Parte1.D0/RX, JP7.1
  N22: Parte1.D1/TX, JP7.2
  N23: U1.Pin_1, R7.Pin_1
  N24: R7.Pin_0, JP5.1

notes:
  Arduino Arcs
  https://www.github.com/pavelmc/arduino-arcs/
  Pavel CO7WT <pavelmc@gmail.com>
  To Si5351 Board I2C
  Si5351 board I2C
  S-Meter Input.
  It is designed to take a sample from a analog moving meter (or where it was) so the value is compared against the 1.1v internal reference for proper dinamic range
  PTT Interface
  Any voltage here indicates that the PTT has ben pressed an we must go to TX, the value of R7 (220) must be calculated to the voltage and opto-coupler used.
  TX-Meter Input.
  Power sensing imput in TX mode, the value is compared against the 1.1v internal reference for proper dinamic range
  Serial Port Interface.
  TTL level Serial Port Interface, for now just for debugging prurposes
